// Logisim project BCD_to_binary.circ as structural Verilog: 3 circuits, main circuit main
module main (
  input  [3:0] A0,
  input  [3:0] A1,
  input  [3:0] A2,
  input  Rst,
  input  Start,
  input  Clk,
  output [9:0] O,
  output E
);

  wire cu_1_add_cnt, cu_1_calc, cu_1_init, cu_1_ld_a, cu_1_ld_cnt, cu_1_ld_out, cu_1_load, dp_1_done;

  Clock clock_1 ();  // open: out
  DP dp_1 (
    .A({A2, A1, A0}), .ld_A(cu_1_ld_a), .ld_out(cu_1_ld_out), .ld_cnt(cu_1_ld_cnt), .add_cnt(cu_1_add_cnt),
    .Rst(Rst), .Start(Start), .INIT(cu_1_init), .LOAD(cu_1_load), .CALC(cu_1_calc), .Clk(Clk),
    .Done(dp_1_done), .O(O), .E(E));
  CU cu_1 (
    .Rst(Rst), .Clk(Clk), .Start(Start), .Done(dp_1_done), .ld_A(cu_1_ld_a), .ld_out(cu_1_ld_out),
    .ld_cnt(cu_1_ld_cnt), .add_cnt(cu_1_add_cnt), .INIT(cu_1_init), .LOAD(cu_1_load), .CALC(cu_1_calc));
endmodule

module CU (
  input  Rst,
  input  Clk,
  input  Start,
  input  Done,
  output ld_A,
  output ld_out,
  output ld_cnt,
  output add_cnt,
  output INIT,
  output LOAD,
  output CALC
);

  wire and_2_out, and_3_out, and_4_out, D_CALC, D_INIT, D_LOAD, not_1_out, not_2_out;

  D_Flip_Flop d_ff_1 (.D(D_INIT), .clk(Clk), .Q(INIT), .preset(Rst));  // open: Qn, reset
  D_Flip_Flop d_ff_2 (.D(D_LOAD), .clk(Clk), .Q(ld_cnt), .reset(Rst));  // open: Qn, preset
  D_Flip_Flop d_ff_3 (.D(D_CALC), .clk(Clk), .Q(add_cnt), .reset(Rst));  // open: Qn, preset
  and and_1 (D_LOAD, INIT, Start);
  and and_2 (and_2_out, add_cnt, not_1_out);
  not not_1 (not_1_out, Done);
  not not_2 (not_2_out, Start);
  and and_3 (and_3_out, INIT, not_2_out);
  and and_4 (and_4_out, add_cnt, Done);
  or or_1 (D_CALC, and_2_out, ld_cnt);
  or or_2 (D_INIT, and_3_out, and_4_out);
  or or_3 (ld_A, ld_cnt, add_cnt);

  assign CALC = add_cnt;
  assign ld_out = ld_A;
  assign LOAD = ld_cnt;
endmodule

module DP (
  input  [11:0] A,
  input  ld_A,
  input  ld_out,
  input  ld_cnt,
  input  add_cnt,
  input  Rst,
  input  Start,
  input  INIT,
  input  LOAD,
  input  CALC,
  input  Clk,
  output Done,
  output [9:0] O,
  output E
);

  wire and_1_out, and_2_out;
  wire [0:0] R_A;
  wire [2:0] A8_11;
  wire [3:0] A0_3, A4_7, adder_1_out, adder_2_out, CNT_q;
  wire [7:0] A_next;
  wire [9:0] D_out;
  wire [11:0] D_A;

  Adder #(.width(4)) adder_1 (.a(A0_3), .b(4'b1101), .out(adder_1_out));  // open: cin, cout
  Adder #(.width(4)) adder_2 (.a(A4_7), .b(4'b1101), .out(adder_2_out));  // open: cin, cout
  Multiplexer #(.width(12)) multiplexer_1 (.in0(A), .in1({1'b0, A8_11, A_next}), .out(D_A), .sel(CALC));
  Multiplexer #(.width(10)) multiplexer_2 (.in0({10{1'b0}}), .in1({R_A[0], O[9:1]}), .out(D_out), .sel(CALC));
  Multiplexer #(.width(4)) multiplexer_3 (.in0(A0_3), .in1(adder_1_out), .out(A_next[3:0]), .sel(A0_3[3]));
  Multiplexer #(.width(4)) multiplexer_4 (.in0(A4_7), .in1(adder_2_out), .out(A_next[7:4]), .sel(A4_7[3]));
  and and_1 (and_1_out, Done, CALC);
  and and_2 (and_2_out, Start, INIT);
  Counter #(.max('hf), .width(4)) CNT (
    .clr(Rst), .load(ld_cnt), .up(1'b1), .count(add_cnt), .clk(Clk), .D(4'b0000), .Q(CNT_q));  // open: carry
  Register #(.width(12)) u_R_A (.D(D_A), .en(ld_A), .clk(Clk), .Q({A8_11, A4_7, A0_3, R_A[0]}), .clr(Rst));
  Register #(.width(10)) R_out (.D(D_out), .en(ld_out), .clk(Clk), .Q(O), .clr(Rst));
  S_R_Flip_Flop s_r_ff_1 (.S(and_1_out), .R(and_2_out), .clk(Clk), .Q(E), .reset(Rst));  // open: Qn, preset
  Comparator #(.width(4)) comparator_1 (.a(CNT_q), .b(4'b1001), .eq(Done));  // open: gt, lt

  // Other names for the same wires on the sheet: R_out[9:0] = O; A_next[10:8] = A8_11;
  //   A_shifted[10:0] = {A8_11, A4_7, A0_3}; R_A[11:1] = {A8_11, A4_7, A0_3}; A3 = A0_3[3]; A7 = A4_7[3]
endmodule
